// Logisim project Somador.circ as structural Verilog: 1 circuit, main circuit main
module main (
);

  wire and_1_out, and_2_out, and_3_out, and_4_out, and_5_out, and_6_out, and_7_out, and_8_out, and_9_out,
       and_10_out, and_11_out, and_12_out, and_13_out, and_14_out, and_15_out, and_16_out, and_17_out,
       and_18_out, and_19_out, and_20_out, not_1_out, not_2_out, not_3_out, not_4_out, or_1_out, or_2_out,
       or_3_out, or_4_out, xnor_1_out, xnor_2_out, xnor_3_out, xnor_4_out, xor_1_out, xor_2_out, xor_3_out,
       xor_4_out;
  wire [0:0] n74283_1_pin9, or_12_out;
  wire [2:0] INPUT_B_out, or_6_out, or_8_out, or_10_out;
  wire [3:0] n74283_1_pin4, or_5_out;

  Slider #(.width(4), .value('hf)) INPUT_A (.out({or_10_out[2], or_8_out[2], or_6_out[2], INPUT_B_out[2]}));
  xnor xnor_1 (xnor_1_out, INPUT_B_out[0], 1'b0);
  xor xor_1 (xor_1_out, INPUT_B_out[0], 1'b0);
  not not_1 (not_1_out, INPUT_B_out[2]);
  and and_1 (and_1_out, INPUT_B_out[0], 1'b0);
  and and_2 (and_2_out, INPUT_B_out[0], INPUT_B_out[2]);
  or or_1 (or_1_out, and_2_out, and_3_out);
  and and_3 (and_3_out, 1'b0, INPUT_B_out[2]);
  xnor xnor_2 (xnor_2_out, or_6_out[0], or_6_out[1]);
  xor xor_2 (xor_2_out, or_6_out[0], or_6_out[1]);
  not not_2 (not_2_out, or_6_out[2]);
  and and_4 (and_4_out, or_6_out[0], or_6_out[1]);
  and and_5 (and_5_out, or_6_out[0], or_6_out[2]);
  or or_2 (or_2_out, and_5_out, and_6_out);
  and and_6 (and_6_out, or_6_out[1], or_6_out[2]);
  xnor xnor_3 (xnor_3_out, or_8_out[0], or_8_out[1]);
  xor xor_3 (xor_3_out, or_8_out[0], or_8_out[1]);
  not not_3 (not_3_out, or_8_out[2]);
  and and_7 (and_7_out, or_8_out[0], or_8_out[1]);
  and and_8 (and_8_out, or_8_out[0], or_8_out[2]);
  or or_3 (or_3_out, and_8_out, and_9_out);
  and and_9 (and_9_out, or_8_out[1], or_8_out[2]);
  xnor xnor_4 (xnor_4_out, or_10_out[0], or_10_out[1]);
  xor xor_4 (xor_4_out, or_10_out[0], or_10_out[1]);
  not not_4 (not_4_out, or_10_out[2]);
  and and_10 (and_10_out, or_10_out[0], or_10_out[1]);
  and and_11 (and_11_out, or_10_out[0], or_10_out[2]);
  or or_4 (or_4_out, and_11_out, and_12_out);
  and and_12 (and_12_out, or_10_out[1], or_10_out[2]);
  Slider #(.width(4)) INPUT_B (.out({or_10_out[1], or_8_out[1], or_6_out[1], INPUT_B_out[0]}));
  and and_13 (and_13_out, xnor_1_out, INPUT_B_out[2]);
  or or_5 (or_5_out[0], and_13_out, and_14_out);
  and and_14 (and_14_out, xor_1_out, not_1_out);
  or or_6 (or_6_out[0], and_1_out, or_1_out);
  and and_15 (and_15_out, xnor_2_out, or_6_out[2]);
  or or_7 (or_5_out[1], and_15_out, and_16_out);
  and and_16 (and_16_out, xor_2_out, not_2_out);
  or or_8 (or_8_out[0], and_4_out, or_2_out);
  and and_17 (and_17_out, xnor_3_out, or_8_out[2]);
  or or_9 (or_5_out[2], and_17_out, and_18_out);
  and and_18 (and_18_out, xor_3_out, not_3_out);
  or or_10 (or_10_out[0], and_7_out, or_3_out);
  and and_19 (and_19_out, xnor_4_out, or_10_out[2]);
  or or_11 (or_5_out[3], and_19_out, and_20_out);
  and and_20 (and_20_out, xor_4_out, not_4_out);
  or or_12 (or_12_out[0], and_10_out, or_4_out);
  Hex_Digit_Display hex_digit_display_1 (.value({3'b000, or_12_out[0]}));  // open: dp
  Hex_Digit_Display hex_digit_display_2 (.value(or_5_out));  // open: dp
  _74283 u_74283_1 (
    .pin1(n74283_1_pin4[1]), .pin2(or_6_out[1]), .pin3(or_6_out[2]), .pin4(n74283_1_pin4[0]),
    .pin5(INPUT_B_out[2]), .pin6(INPUT_B_out[0]), .pin15(or_8_out[1]), .pin14(or_8_out[2]),
    .pin13(n74283_1_pin4[2]), .pin12(or_10_out[2]), .pin11(or_10_out[1]), .pin10(n74283_1_pin4[3]),
    .pin9(n74283_1_pin9[0]));  // open: pin7
  _7408 u_7408_1 ();  // open: pin1, pin2, pin3, pin4, pin5, pin6, pin13, pin12, pin11, pin10, pin9, pin8
  _7404 u_7404_1 ();  // open: pin1, pin2, pin3, pin4, pin5, pin6, pin13, pin12, pin11, pin10, pin9, pin8
  Hex_Digit_Display hex_digit_display_3 (.value(n74283_1_pin4));  // open: dp
  Hex_Digit_Display hex_digit_display_4 (.value({3'b000, n74283_1_pin9[0]}));  // open: dp
  _7486 u_7486_1 ();  // open: pin1, pin2, pin3, pin4, pin5, pin6, pin13, pin12, pin11, pin10, pin9, pin8
  _7408 u_7408_2 ();  // open: pin1, pin2, pin3, pin4, pin5, pin6, pin13, pin12, pin11, pin10, pin9, pin8
  _7432 u_7432_1 ();  // open: pin1, pin2, pin3, pin4, pin5, pin6, pin13, pin12, pin11, pin10, pin9, pin8
  _7404 u_7404_2 ();  // open: pin1, pin2, pin3, pin4, pin5, pin6, pin13, pin12, pin11, pin10, pin9, pin8
  _7486 u_7486_2 ();  // open: pin1, pin2, pin3, pin4, pin5, pin6, pin13, pin12, pin11, pin10, pin9, pin8
  _7408 u_7408_3 ();  // open: pin1, pin2, pin3, pin4, pin5, pin6, pin13, pin12, pin11, pin10, pin9, pin8
  _7432 u_7432_2 ();  // open: pin1, pin2, pin3, pin4, pin5, pin6, pin13, pin12, pin11, pin10, pin9, pin8
  _7408 u_7408_4 ();  // open: pin1, pin2, pin3, pin4, pin5, pin6, pin13, pin12, pin11, pin10, pin9, pin8
  _7432 u_7432_3 ();  // open: pin1, pin2, pin3, pin4, pin5, pin6, pin13, pin12, pin11, pin10, pin9, pin8
  _7408 u_7408_5 ();  // open: pin1, pin2, pin3, pin4, pin5, pin6, pin13, pin12, pin11, pin10, pin9, pin8

  // Notes on the sheet:
  //   OUTPUT
  //   OUTPUT
endmodule
