// Logisim project SomadorCIs.circ as structural Verilog: 1 circuit, main circuit main
module main (
);

  wire [3:0] INPUT_A_out, INPUT_B_out, undriven, undriven_2;

  Hex_Digit_Display hex_digit_display_1 (.value(undriven));  // open: dp
  Hex_Digit_Display hex_digit_display_2 (.value(undriven_2));  // open: dp
  _7486 u_7486_1 ();  // open: pin1, pin2, pin3, pin4, pin5, pin6, pin13, pin12, pin11, pin10, pin9, pin8
  _7408 u_7408_1 ();  // open: pin1, pin2, pin3, pin4, pin5, pin6, pin13, pin12, pin11, pin10, pin9, pin8
  _7486 u_7486_2 ();  // open: pin1, pin2, pin3, pin4, pin5, pin6, pin13, pin12, pin11, pin10, pin9, pin8
  Slider #(.width(4), .value('hf)) INPUT_A (.out(INPUT_A_out));
  Slider #(.width(4)) INPUT_B (.out(INPUT_B_out));
  _7408 u_7408_2 ();  // open: pin1, pin2, pin3, pin4, pin5, pin6, pin13, pin12, pin11, pin10, pin9, pin8
  _7432 u_7432_1 ();  // open: pin1, pin2, pin3, pin4, pin5, pin6, pin13, pin12, pin11, pin10, pin9, pin8

  // Notes on the sheet:
  //   OUTPUT
endmodule
